# Fritzing sketch Banana Bongos (saved by Fritzing 0.9.3b)
breadboards: 1

parts:
  Part1 = Arduino Mega 2560 (Rev3)
  R1 = Resistor [tolerance=±5% resistance=1M package=THT]
  R2 = Resistor [tolerance=±5% resistance=1M package=THT]
  R3 = Resistor [tolerance=±5% resistance=1M package=THT]
  R4 = Resistor [tolerance=±5% resistance=1M package=THT]
  R5 = Resistor [tolerance=±5% resistance=1M package=THT]
  R6 = Resistor [tolerance=±5% resistance=1M package=THT]
  CLIP2 = Alligator Clip
  CLIP6 = Alligator Clip
  CLIP1 = Alligator Clip
  CLIP3 = Alligator Clip
  CLIP4 = Alligator Clip
  CLIP5 = Alligator Clip

nets:
  N1: Part1.D13_PWM, R1.Pin_0
  N2: Part1.D12_PWM, R1.Pin_1, CLIP1.wire
  N3: Part1.D11_PWM, R2.Pin_0
  N4: Part1.D10_PWM, R2.Pin_1, CLIP2.wire
  N5: Part1.D9_PWM, R3.Pin_0
  N6: Part1.D8_PWM, R3.Pin_1, CLIP3.wire
  N7: Part1.D2_PWM, R6.Pin_1, CLIP6.wire
  N8: Part1.D3_PWM, R6.Pin_0
  N9: Part1.D4_PWM, R5.Pin_1, CLIP5.wire
  N10: Part1.D5_PWM, R5.Pin_0
  N11: Part1.D6_PWM, R4.Pin_1, CLIP4.wire
  N12: Part1.D7_PWM, R4.Pin_0

custom parts:
  Alligator Clip: Alligator clip
  Alligator Clip: Alligator clip
  Alligator Clip: Alligator clip
  Alligator Clip: Alligator clip
  Alligator Clip: Alligator clip
  Alligator Clip: Alligator clip
